// Logisim project Lab5.circ as structural Verilog: 1 circuit, main circuit main
module main (
  input  [3:0] A,
  input  [3:0] B,
  input  sub
);

  wire adder_1_cout, and_1_out, and_2_out, and_3_out, nor_1_out, SOV, UOV, xor_3_p2;
  wire [3:0] Mux_O, not_1_out, O;

  // Probe on A
  // Probe on B
  // Probe on O
  LED led_1 (.in(UOV));
  // Probe on A
  // Probe on B
  // Probe on O
  LED led_2 (.in(SOV));
  Multiplexer #(.width(4)) multiplexer_1 (.in0(B), .in1(not_1_out), .out(Mux_O), .sel(sub));  // open: en
  assign not_1_out = ~B;  // NOT_Gate not_1, 4 bits wide
  nor nor_1 (nor_1_out, A[3], Mux_O[3]);
  and and_1 (and_1_out, A[3], Mux_O[3]);
  and and_2 (and_2_out, A[3], Mux_O[3], O[3]);
  xor xor_1 (SOV, and_2_out, xor_3_p2);
  Adder #(.width(4)) adder_1 (.a(A), .b(Mux_O), .out(O), .cin(sub), .cout(adder_1_cout));
  // XOR_Gate xor_2: pin names not known; wires that end beside it: adder_1_cout, sub, UOV
  and and_3 (and_3_out, nor_1_out, O[3]);
  // XOR_Gate xor_3: pin names not known; wires that end beside it: and_1_out, xor_3_p2, and_3_out

  // Other names for the same wires on the sheet: SA = A[3]; SB = Mux_O[3]; SO = O[3]
endmodule
