// Logisim project Lab6.circ as structural Verilog: 1 circuit, main circuit main
module main (
);

  wire button_1_out, CLK, clock_1_out, count____7, decoder_1_out0, decoder_1_out1, decoder_1_out2,
       decoder_1_out3, decoder_1_out4, decoder_1_out5, decoder_1_out6, decoder_1_out7, decoder_1_out8,
       decoder_1_out9, decoder_1_out10, decoder_1_out11, decoder_1_out12, decoder_1_out13, decoder_1_out14,
       decoder_1_out15, lose, not_1_out, stop, win;
  wire [3:0] adder_1_out, Count;

  Clock clock_1 (.out(clock_1_out));
  Button button_1 (.out(button_1_out));
  LED led_1 (.in(decoder_1_out0));
  or or_1 (CLK, clock_1_out, button_1_out);
  LED led_2 (.in(decoder_1_out1));
  LED led_3 (.in(decoder_1_out3));
  LED led_4 (.in(decoder_1_out2));
  LED led_5 (.in(decoder_1_out4));
  Decoder #(.select(4)) decoder_1 (
    .out0(decoder_1_out0), .out1(decoder_1_out1), .out2(decoder_1_out2), .out3(decoder_1_out3),
    .out4(decoder_1_out4), .out5(decoder_1_out5), .out6(decoder_1_out6), .out7(decoder_1_out7),
    .out8(decoder_1_out8), .out9(decoder_1_out9), .out10(decoder_1_out10), .out11(decoder_1_out11),
    .out12(decoder_1_out12), .out13(decoder_1_out13), .out14(decoder_1_out14), .out15(decoder_1_out15),
    .sel(Count));  // open: en
  Register #(.width(4)) register_1 (.D(adder_1_out), .en(not_1_out), .Q(Count), .clk(CLK));  // open: clr
  Adder #(.width(4)) adder_1 (.a(Count), .b(4'b0001), .out(adder_1_out));  // open: cin, cout
  not not_1 (not_1_out, stop);
  Button button_2 (.out(stop));
  LED led_6 (.in(decoder_1_out6));
  LED led_7 (.in(decoder_1_out5));
  LED led_8 (.in(decoder_1_out8));
  LED led_9 (.in(decoder_1_out7));
  LED led_10 (.in(decoder_1_out12));
  LED led_11 (.in(decoder_1_out9));
  LED led_12 (.in(decoder_1_out10));
  LED led_13 (.in(decoder_1_out11));
  Comparator #(.width(4)) comparator_1 (.a(Count), .b(4'b0111), .eq(count____7));  // open: gt, lt
  LED led_14 (.in(win));
  LED led_15 (.in(lose));
  LED led_16 (.in(decoder_1_out14));
  LED led_17 (.in(decoder_1_out15));
  LED led_18 (.in(decoder_1_out13));
  and and_1 (win, stop, stop, count____7, count____7);
  ExactlyOne xor_1 (.out(lose), .in0(stop), .in1(stop), .in3(count____7), .in4(count____7));

  // Notes on the sheet:
  //   V
  //   Win
  //   Lose
endmodule
