// Logisim project Lab7.circ as structural Verilog: 3 circuits, main circuit main
module main (
  input  [7:0] ALU_A,
  input  [7:0] ALU_B,
  input  [2:0] ALU_Op,
  input  [7:0] REG_rd,
  input  [2:0] rd,
  input  Reg_WE,
  input  [2:0] rs,
  input  [2:0] rt
);

  wire CLK, clock_1_out, tick_out;
  wire [7:0] ALU_Out, REG_rs, REG_rt;

  Clock clock_1 (.out(clock_1_out));
  or or_1 (CLK, clock_1_out, tick_out);
  Button tick (.out(tick_out));
  // Probe on ALU_A
  // Probe on ALU_B
  // Probe on ALU_Out
  // Probe on REG_rd
  // Probe on REG_rs
  // Probe on REG_rt
  ALU ALU (.A(ALU_A), .B(ALU_B), .ALU_Op(ALU_Op), .ALU_Out(ALU_Out));
  Register_File register_file_1 (
    .CLK(CLK), .REG_rd(REG_rd), .rs(rs), .Reg_WE(Reg_WE), .rd(rd), .rt(rt), .REG_rs(REG_rs), .REG_rt(REG_rt));
endmodule

module ALU (
  input  [7:0] A,
  input  [7:0] B,
  input  [2:0] ALU_Op,
  output [7:0] ALU_Out
);

  wire [2:0] bit_extender_1_out;
  wire [7:0] adder_1_out, and_1_out, not_1_out, or_1_out, Shift_left, Shift_right, subtractor_1_out,
       undriven, xor_1_out;

  Subtractor subtractor_1 (.a(A), .b(B), .out(subtractor_1_out));  // open: bin, bout
  Adder adder_1 (.a(A), .b(B), .out(adder_1_out));  // open: cin, cout
  assign or_1_out = undriven | A | B;  // OR_Gate or_1, 8 bits wide
  assign and_1_out = A & B & undriven;  // AND_Gate and_1, 8 bits wide
  // NOT_Gate not_1 has open pins: in=open, out=not_1_out
  Multiplexer #(.select(3), .width(8)) multiplexer_1 (
    .in0(adder_1_out), .in1(subtractor_1_out), .in2(and_1_out), .in3(or_1_out), .in4(xor_1_out),
    .in5(not_1_out), .in6(Shift_left), .in7(Shift_right), .out(ALU_Out), .sel(ALU_Op));  // open: en
  assign xor_1_out = A ^ B;  // XOR_Gate xor_1, 8 bits wide
  Bit_Extender #(.out_width(3)) bit_extender_1 (.in(B), .out(bit_extender_1_out));
  Shifter shifter_1 (.in(A), .\dist (bit_extender_1_out), .out(Shift_left));
  Shifter #(.shift("lr")) shifter_2 (.in(A), .\dist (bit_extender_1_out), .out(Shift_right));
endmodule

module Register_File (
  input  CLK,
  input  [7:0] REG_rd,
  input  [2:0] rs,
  input  Reg_WE,
  input  [2:0] rd,
  input  [2:0] rt,
  output [7:0] REG_rs,
  output [7:0] REG_rt
);

  wire demultiplexer_1_out1, demultiplexer_1_out2, demultiplexer_1_out3, demultiplexer_1_out4,
       demultiplexer_1_out5, demultiplexer_1_out6, demultiplexer_1_out7;
  wire [7:0] _1, _2, _3, _4, _5, _6, _7;

  Demultiplexer #(.select(3)) demultiplexer_1 (
    .out1(demultiplexer_1_out1), .out2(demultiplexer_1_out2), .out3(demultiplexer_1_out3),
    .out4(demultiplexer_1_out4), .out5(demultiplexer_1_out5), .out6(demultiplexer_1_out6),
    .out7(demultiplexer_1_out7), .in(Reg_WE), .sel(rd));  // open: out0, en
  // Register register_1: pin names not known; wires that end beside it: REG_rd, demultiplexer_1_out1, CLK, _1
  // Register register_2: pin names not known; wires that end beside it: REG_rd, demultiplexer_1_out2, CLK, _2
  // Register register_3: pin names not known; wires that end beside it: REG_rd, demultiplexer_1_out3, CLK, _3
  // Register register_4: pin names not known; wires that end beside it: REG_rd, demultiplexer_1_out4, CLK, _4
  // Register register_5: pin names not known; wires that end beside it: REG_rd, demultiplexer_1_out5, CLK, _5
  // Register register_6: pin names not known; wires that end beside it: REG_rd, demultiplexer_1_out6, CLK, _6
  // Register register_7: pin names not known; wires that end beside it: REG_rd, demultiplexer_1_out7, CLK, _7
  Multiplexer #(.select(3), .width(8)) multiplexer_1 (
    .in0({8{1'b0}}), .in1(_1), .in2(_2), .in3(_3), .in4(_4), .in5(_5), .in6(_6), .in7(_7), .out(REG_rs),
    .sel(rs));  // open: en
  Multiplexer #(.select(3), .width(8)) multiplexer_2 (
    .in0({8{1'b0}}), .in1(_1), .in2(_2), .in3(_3), .in4(_4), .in5(_5), .in6(_6), .in7(_7), .out(REG_rt),
    .sel(rt));  // open: en
endmodule
