// Logisim project ecd57_proj2.circ as structural Verilog: 7 circuits, main circuit main
module main (
);

  wire B, B_Enable, button_1_out, CLK, clock_1_out, halt, J, J_op, Put, Ram_WE, Reg_WE;
  wire [1:0] B_op;
  wire [2:0] rd, RegDataSrc, rs, rt;
  wire [3:0] ALU_op, display_unit_1_digit0, display_unit_1_digit1, display_unit_1_digit2,
       display_unit_1_digit3;
  wire [7:0] alu, imm, multiplexer_1_out, multiplexer_2_out, PC_1, pc_fsm_1_pc_out, RAM_Out, REG_rs, REG_rt;
  wire [21:0] rom_1_data;

  Clock clock_1 (.out(clock_1_out));
  Button button_1 (.out(button_1_out));
  or or_1 (CLK, clock_1_out, button_1_out);
  Branch_Comparator Branch_Comp (.REG_rs(REG_rs), .REG_rt(REG_rt), .B_op(B_op), .Branch(B), .B_Enable(B_Enable));
  Display_Unit display_unit_1 (
    .Data_Lo(REG_rt), .Data_Hi(REG_rs), .Display_WE(Put), .CLK(CLK), .Digit0(display_unit_1_digit0),
    .Digit1(display_unit_1_digit1), .Digit2(display_unit_1_digit2), .Digit3(display_unit_1_digit3));
  Multiplexer #(.width(8)) multiplexer_1 (.in0(imm), .in1(REG_rs), .out(multiplexer_1_out), .sel(J_op));  // open: en
  ALU alu_1 (.rs(REG_rs), .rt(REG_rt), .ALU_Op(ALU_op), .ALU_Out(alu), .Intermediate(imm));
  Hex_Digit_Display hex_digit_display_1 (.value(display_unit_1_digit2));  // open: dp
  Hex_Digit_Display hex_digit_display_2 (.value(display_unit_1_digit3));  // open: dp
  PC_FSM pc_fsm_1 (
    .CLK(CLK), .Target(multiplexer_1_out), .Jump(J), .Branch(B), .Halt(halt), .Offset(imm),
    .PC_Out(pc_fsm_1_pc_out), .PC_1_Out(PC_1));
  Hex_Digit_Display hex_digit_display_3 (.value(display_unit_1_digit1));  // open: dp
  Hex_Digit_Display hex_digit_display_4 (.value(display_unit_1_digit0));  // open: dp
  // Probe on pc_fsm_1_pc_out
  Multiplexer #(.select(3), .width(8)) multiplexer_2 (
    .in0(alu), .in1(imm), .in2(REG_rs), .in3(RAM_Out), .in4(PC_1), .out(multiplexer_2_out), .sel(RegDataSrc));  // open: in5, in6, in7, en
  LED u_HALT (.in(halt));
  Register_File register_file_1 (
    .CLK(CLK), .REG_rd(multiplexer_2_out), .rs(rs), .Reg_WE(Reg_WE), .rd(rd), .rt(rt), .REG_rs(REG_rs),
    .REG_rt(REG_rt));
  ROM #(.dataWidth(22)) rom_1 (.addr(pc_fsm_1_pc_out), .data(rom_1_data));  // open: sel
  RAM #(.bus("separate")) ram_1 (
    .addr(alu), .din(REG_rt), .data(RAM_Out), .str(Ram_WE), .clk(CLK));  // open: sel, ld, clr
  Control control_1 (
    .Instruction_Input(rom_1_data), .rs(rs), .rt(rt), .halt(halt), .Display_WE(Put), .imm(imm),
    .Reg_WE(Reg_WE), .RegDataSrc(RegDataSrc), .ALU_op(ALU_op), .RAM_WE(Ram_WE), .Jump(J), .J_Op(J_op),
    .rd(rd), .B_op(B_op), .Branch(B_Enable));

  // Notes on the sheet:
  //   InstMem
  //   contents of rom_1 (hex, n*v repeats v):
  //   40101 40202 40303 2c0710 24000 2c0710 28000 2c070a 2c000 0 bf000 1c3601 2c0710 1e3601 83700 2e3800
  //   20000 2e3800
endmodule

module ALU (
  input  [7:0] rs,
  input  [7:0] rt,
  input  [3:0] ALU_Op,
  input  [7:0] Intermediate,
  output [7:0] ALU_Out
);

  wire [2:0] bit_extender_1_out, bit_extender_2_out;
  wire [7:0] Add, Adi, And, Ani, Not, Or, Ori, Sbi, Shl, Shr, Sli, Sri, Sub, Xor, Xri;

  assign And = rt & rs;  // AND_Gate and_1, 8 bits wide
  // OR_Gate #(.width(8)) or_1: pin names not known; wires that end beside it: rt, rs, Or
  // NOT_Gate not_1 has open pins: in=open, out=Not
  Bit_Extender #(.out_width(3)) bit_extender_1 (.in(rt), .out(bit_extender_1_out));
  Subtractor subtractor_1 (.a(rs), .b(rt), .out(Sub));  // open: bin, bout
  Adder adder_1 (.a(rs), .b(rt), .out(Add));  // open: cin, cout
  assign Xor = rt ^ rs;  // XOR_Gate xor_1, 8 bits wide
  Shifter shifter_1 (.in(rs), .\dist (bit_extender_1_out), .out(Shl));
  Shifter #(.shift("lr")) shifter_2 (.in(rs), .\dist (bit_extender_1_out), .out(Shr));
  Subtractor subtractor_2 (.a(rs), .b(Intermediate), .out(Sbi));  // open: bin, bout
  Adder adder_2 (.a(rs), .b(Intermediate), .out(Adi));  // open: cin, cout
  assign Ani = rs & Intermediate;  // AND_Gate and_2, 8 bits wide
  // OR_Gate #(.width(8)) or_2: pin names not known; wires that end beside it: rs, Intermediate, Ori
  assign Xri = Intermediate ^ rs;  // XOR_Gate xor_2, 8 bits wide
  Shifter shifter_3 (.in(rs), .\dist (bit_extender_2_out), .out(Sli));
  Bit_Extender #(.out_width(3)) bit_extender_2 (.in(Intermediate), .out(bit_extender_2_out));
  Shifter #(.shift("lr")) shifter_4 (.in(rs), .\dist (bit_extender_2_out), .out(Sri));
  Multiplexer #(.select(4), .width(8)) multiplexer_1 (
    .in0(Add), .in1(Sub), .in2(And), .in3(Or), .in4(Xor), .in5(Not), .in6(Shl), .in7(Shr), .in8(Adi),
    .in9(Sbi), .in10(Ani), .in11(Ori), .in12(Xri), .in13(Sli), .in14(Sri), .out(ALU_Out), .sel(ALU_Op));  // open: in15, en

  // Other names for the same wires on the sheet: ALUop[3:0] = ALU_Op; Imm[7:0] = Intermediate
endmodule

module Display_Unit (
  input  [7:0] Data_Lo,
  input  [7:0] Data_Hi,
  input  Display_WE,
  input  CLK,
  output [3:0] Digit0,
  output [3:0] Digit1,
  output [3:0] Digit2,
  output [3:0] Digit3
);

  Register #(.width(16)) register_1 (
    .D({Data_Hi, Data_Lo}), .en(Display_WE), .Q({Digit3, Digit2, Digit1, Digit0}), .clk(CLK));  // open: clr
endmodule

module Register_File (
  input  CLK,
  input  [7:0] REG_rd,
  input  [2:0] rs,
  input  Reg_WE,
  input  [2:0] rd,
  input  [2:0] rt,
  output [7:0] REG_rs,
  output [7:0] REG_rt
);

  wire demultiplexer_1_out1, demultiplexer_1_out2, demultiplexer_1_out3, demultiplexer_1_out4,
       demultiplexer_1_out5, demultiplexer_1_out6, demultiplexer_1_out7;
  wire [7:0] _1, _2, _3, _4, _5, _6, _7;

  Demultiplexer #(.select(3)) demultiplexer_1 (
    .out1(demultiplexer_1_out1), .out2(demultiplexer_1_out2), .out3(demultiplexer_1_out3),
    .out4(demultiplexer_1_out4), .out5(demultiplexer_1_out5), .out6(demultiplexer_1_out6),
    .out7(demultiplexer_1_out7), .in(Reg_WE), .sel(rd));  // open: out0, en
  // Register register_1: pin names not known; wires that end beside it: REG_rd, demultiplexer_1_out1, CLK, _1
  // Register register_2: pin names not known; wires that end beside it: REG_rd, demultiplexer_1_out2, CLK, _2
  // Register register_3: pin names not known; wires that end beside it: REG_rd, demultiplexer_1_out3, CLK, _3
  // Register register_4: pin names not known; wires that end beside it: REG_rd, demultiplexer_1_out4, CLK, _4
  // Register register_5: pin names not known; wires that end beside it: REG_rd, demultiplexer_1_out5, CLK, _5
  // Register register_6: pin names not known; wires that end beside it: REG_rd, demultiplexer_1_out6, CLK, _6
  // Register register_7: pin names not known; wires that end beside it: REG_rd, demultiplexer_1_out7, CLK, _7
  Multiplexer #(.select(3), .width(8)) multiplexer_1 (
    .in0({8{1'b0}}), .in1(_1), .in2(_2), .in3(_3), .in4(_4), .in5(_5), .in6(_6), .in7(_7), .out(REG_rs),
    .sel(rs));  // open: en
  Multiplexer #(.select(3), .width(8)) multiplexer_2 (
    .in0({8{1'b0}}), .in1(_1), .in2(_2), .in3(_3), .in4(_4), .in5(_5), .in6(_6), .in7(_7), .out(REG_rt),
    .sel(rt));  // open: en
endmodule

module PC_FSM (
  input  CLK,
  input  [7:0] Target,
  input  Jump,
  input  Branch,
  input  Halt,
  input  [7:0] Offset,
  output [7:0] PC_Out,
  output [7:0] PC_1_Out
);

  wire Halt_t;
  wire [7:0] multiplexer_1_out, multiplexer_2_out;

  // NOT_Gate not_1 has open pins: in=open, out=Halt_t
  Adder adder_1 (.a(PC_Out), .b(multiplexer_1_out), .out(PC_1_Out));  // open: cin, cout
  Multiplexer #(.width(8)) multiplexer_1 (.in0(8'h1), .in1(Offset), .out(multiplexer_1_out), .sel(Branch));  // open: en
  Multiplexer #(.width(8)) multiplexer_2 (
    .in0(PC_1_Out), .in1(Target), .out(multiplexer_2_out), .sel(Jump));  // open: en
  Register PC (.D(multiplexer_2_out), .en(Halt_t), .Q(PC_Out), .clk(CLK));  // open: clr
endmodule

module Control (
  input  [21:0] Instruction_Input,
  output [2:0] rd,
  output [2:0] rs,
  output [2:0] rt,
  output halt,
  output Display_WE,
  output [7:0] imm,
  output Reg_WE,
  output RAM_WE,
  output Jump,
  output [2:0] RegDataSrc,
  output [3:0] ALU_op,
  output Branch,
  output J_Op,
  output [1:0] B_op
);

  wire add, adi, \and , ani, beq, bge, blt, bne, j, jal, jr, ld, li, mov, \not , \or , or_1_out, or_3_out,
       ori, sbi, shl, shr, sli, sri, sub, \xor , xri;

  or or_1 (or_1_out, ld, RAM_WE, adi);
  or or_2 (Reg_WE, mov, li, ld, add, sub, \and , \or , \xor , \not , shl, shr, adi, sbi, ani, ori, xri, sli, sri, jal);
  Priority_Encoder #(.select(4)) priority_encoder_1 (
    .in0(add), .in1(sub), .in2(\and ), .in3(\or ), .in4(\xor ), .in5(\not ), .in6(shl), .in7(shr),
    .in8(or_1_out), .in9(sbi), .in10(ani), .in11(ori), .in12(xri), .in13(sli), .in14(sri), .out(ALU_op));  // open: in15, gs, en_out, en_in
  Decoder #(.select(5)) decoder_1 (
    .out0(halt), .out1(Display_WE), .out2(li), .out3(mov), .out4(ld), .out5(RAM_WE), .out6(add), .out7(sub),
    .out8(\and ), .out9(\or ), .out10(\xor ), .out11(\not ), .out12(shl), .out13(shr), .out14(adi),
    .out15(sbi), .out16(ani), .out17(ori), .out18(xri), .out19(sli), .out20(sri), .out21(j), .out22(jal),
    .out23(jr), .out24(blt), .out25(bge), .out26(beq), .out27(bne), .sel(Instruction_Input[21:17]));  // open: out28, out29, out30, out31, en
  Priority_Encoder priority_encoder_2 (
    .in0(1'b1), .in1(li), .in2(mov), .in3(ld), .in4(jal), .out(RegDataSrc));  // open: in5, in6, in7, en_in, gs, en_out
  or or_3 (or_3_out, j, jal);
  Priority_Encoder #(.select(1)) priority_encoder_3 (.in0(or_3_out), .in1(jr), .out(J_Op));  // open: gs, en_out, en_in
  Priority_Encoder #(.select(2)) priority_encoder_4 (
    .in0(blt), .in1(bge), .in2(beq), .in3(bne), .out(B_op));  // open: gs, en_out, en_in
  or or_4 (Jump, j, jr, jal);
  or or_5 (Branch, blt, bge, beq, bne);

  assign imm = Instruction_Input[7:0];
  assign rd = Instruction_Input[10:8];
  assign rs = Instruction_Input[13:11];
  assign rt = Instruction_Input[16:14];

  // Other names for the same wires on the sheet: hlt = halt; opcode[4:0] = Instruction_Input[21:17]; put = Display_WE;
  //   st = RAM_WE
endmodule

module Branch_Comparator (
  input  [7:0] REG_rs,
  input  [7:0] REG_rt,
  input  [1:0] B_op,
  input  B_Enable,
  output Branch
);

  wire beq, bge, blt, bne, comparator_2_eq, comparator_2_gt, comparator_2_lt;

  Comparator comparator_1 (.a(REG_rs), .b(REG_rt), .eq(beq), .lt(blt));  // open: gt
  or or_1 (bge, comparator_2_gt, comparator_2_eq, comparator_2_lt);
  Comparator comparator_2 (.a(REG_rs), .b(REG_rt), .gt(comparator_2_gt), .eq(comparator_2_eq), .lt(comparator_2_lt));
  // NOT_Gate not_1: pin names not known; wires that end beside it: comparator_2_eq, bne, comparator_2_gt, comparator_2_eq
  Multiplexer #(.select(2), .enable("true")) multiplexer_1 (
    .in0(blt), .in1(bge), .in2(beq), .in3(bne), .out(Branch), .sel(B_op), .en(B_Enable));

  // Other names for the same wires on the sheet: Rs[7:0] = REG_rs; Rt[7:0] = REG_rt
endmodule
